# Fritzing sketch 32x8_led_banner (saved by Fritzing 0.8.7b)
breadboards: 3

parts:
  U1 = MAX7219 [package=dil24]
  U2 = MAX7219 [package=dil24]
  U3 = MAX7219 [package=dil24]
  U4 = MAX7219 [package=dil24]
  R1 = Resistor [tolerance=±5% resistance=10k package=THT]
  R2 = Resistor [tolerance=±5% resistance=10k package=THT]
  R3 = Resistor [tolerance=±5% resistance=10k package=THT]
  R4 = Resistor [tolerance=±5% resistance=10k package=THT]
  Raspberry_Pi_B_rev1 = Raspberry Pi B rev2
  8x8_LED_Matrix1 = 8x8 LED Matrix 1588ASR
  8x8_LED_Matrix2 = 8x8 LED Matrix 1588ASR
  8x8_LED_Matrix3 = 8x8 LED Matrix 1588ASR
  8x8_LED_Matrix4 = 8x8 LED Matrix 1588ASR

nets:
  N1: U1.DIN, Raspberry_Pi_B_rev1.GPIO_10
  N2: U1.DIG4, 8x8_LED_Matrix1.Pin_2
  GND: U1.GND, U1.GND2, U2.GND, U2.GND2, U3.GND, U3.GND2, U4.GND, U4.GND2, Raspberry_Pi_B_rev1.GND
  N3: U1.DIG2, 8x8_LED_Matrix1.Pin_16
  N4: U1.DIG3, 8x8_LED_Matrix1.Pin_15
  N5: U1.DIG5, 8x8_LED_Matrix1.Pin_1
  N6: U1.LOAD, U2.LOAD, U3.LOAD, U4.LOAD, Raspberry_Pi_B_rev1.GPIO_8
  N7: U1.CLK, U2.CLK, U3.CLK, U4.CLK, Raspberry_Pi_B_rev1.GPIO_11
  N8: U1.SEGA, 8x8_LED_Matrix1.Pin_13
  N9: U1.SEGB, 8x8_LED_Matrix1.Pin_12
  N10: U1.ISET, R1.Pin_0
  VCC: U1.VCC, U2.VCC, U3.VCC, U4.VCC, R1.Pin_1, R2.Pin_1, R3.Pin_1, R4.Pin_1, Raspberry_Pi_B_rev1.5V
  N11: U1.SEGC, 8x8_LED_Matrix1.Pin_11
  N12: U1.SEGE, 8x8_LED_Matrix1.Pin_9
  N13: U1.SEGDP, 8x8_LED_Matrix1.Pin14
  N14: U1.SEGD, 8x8_LED_Matrix1.Pin_10
  N15: U1.DOUT, U2.DIN
  N16: U2.DIG4, 8x8_LED_Matrix2.Pin_2
  N17: U2.DIG2, 8x8_LED_Matrix2.Pin_16
  N18: U2.DIG3, 8x8_LED_Matrix2.Pin_15
  N19: U2.DIG5, 8x8_LED_Matrix2.Pin_1
  N20: U2.SEGA, 8x8_LED_Matrix2.Pin_13
  N21: U2.SEGB, 8x8_LED_Matrix2.Pin_12
  N22: U2.ISET, R2.Pin_0
  N23: U2.SEGC, 8x8_LED_Matrix2.Pin_11
  N24: U2.SEGE, 8x8_LED_Matrix2.Pin_9
  N25: U2.SEGDP, 8x8_LED_Matrix2.Pin14
  N26: U2.SEGD, 8x8_LED_Matrix2.Pin_10
  N27: U2.DOUT, U3.DIN
  N28: U3.DIG4, 8x8_LED_Matrix3.Pin_2
  N29: U3.DIG2, 8x8_LED_Matrix3.Pin_16
  N30: U3.DIG3, 8x8_LED_Matrix3.Pin_15
  N31: U3.DIG5, 8x8_LED_Matrix3.Pin_1
  N32: U3.SEGA, 8x8_LED_Matrix3.Pin_13
  N33: U3.SEGB, 8x8_LED_Matrix3.Pin_12
  N34: U3.ISET, R3.Pin_0
  N35: U3.SEGC, 8x8_LED_Matrix3.Pin_11
  N36: U3.SEGE, 8x8_LED_Matrix3.Pin_9
  N37: U3.SEGDP, 8x8_LED_Matrix3.Pin14
  N38: U3.SEGD, 8x8_LED_Matrix3.Pin_10
  N39: U3.DOUT, U4.DIN
  N40: U4.DIG0, 8x8_LED_Matrix4.Pin_1
  N41: U4.DIG2, 8x8_LED_Matrix4.Pin_16
  N42: U4.SEGF, 8x8_LED_Matrix4.Pin14
  N43: U4.SEGB, 8x8_LED_Matrix4.Pin_9
  N44: U4.SEGG, 8x8_LED_Matrix4.Pin_13
  N45: U4.ISET, R4.Pin_0
  N46: U4.SEGE, 8x8_LED_Matrix4.Pin_12
  N47: U4.SEGDP, 8x8_LED_Matrix4.Pin_10
  N48: U4.SEGD, 8x8_LED_Matrix4.Pin_15
  N49: U4.DOUT, 8x8_LED_Matrix4.Pin_11

custom parts:
  8x8 LED Matrix 1588ASR: Red Color Common cathode 8x8 LED Matrix
